# Fritzing sketch me (saved by Fritzing 0.9.3b)

parts:
  U1 = LuaNode32 / ESP32 [part_number=ESP32S-PIN30]
  U2 = Texas Instruments DRV8833
  U3 = Texas Instruments DRV8833
  U4 = Texas Instruments DRV8833
  M1 = DC Mini Metal Gear Motor
  M2 = DC Mini Metal Gear Motor
  M3 = DC Mini Metal Gear Motor
  M4 = DC Mini Metal Gear Motor
  M5 = DC Mini Metal Gear Motor
  M6 = DC Mini Metal Gear Motor
  U5 = Texas Instruments DRV8833
  VCC1 = Battery block 9V
  U6 = SWITCH_SPDT [package=kps-1290]
  A1 = ky-033 [package=THT]
  A2 = ky-033 [package=THT]
  Part1 = Adafruit TCS34725 RGB Color Sensor [part_number="Adafruit #1334"]

nets:
  N1: U1.D32, U3.IN1
  N2: U1.D33, U3.IN2
  N3: U1.D25, U3.IN3
  N4: U1.D26, U3.IN4
  N5: U1.D27, U2.IN1
  N6: U1.D14, U4.IN2
  N7: U1.D12, U4.IN3
  N8: U1.D13, U4.IN4
  N9: U1.GND, VCC1.-, A2.pin3
  N10: U1.Vin, U6.P
  N11: U1.D2, Part1.LED_EN
  N12: U1.D4, A2.pin2
  N13: U1.RX2, A1.pin2
  N14: U1.TX2, U5.IN2
  N15: U1.D18, U5.IN3
  N16: U1.D19, U5.IN1
  N17: U1.D21, Part1.SDA
  N18: U1.D22, Part1.SCL
  N19: U1.D23, U5.IN4
  N20: U3.OUT1, M1.IN1
  N21: U3.OUT2, M1.IN2
  N22: U3.OUT3, M2.IN1
  N23: U3.OUT4, M2.IN2
  N24: U4.OUT1, M5.IN1
  N25: U4.OUT2, M5.IN2
  N26: U4.OUT3, M6.IN1
  N27: U4.OUT4, M6.IN2
  N28: M3.IN1, U5.OUT1
  N29: M3.IN2, U5.OUT2
  N30: M4.IN1, U5.OUT3
  N31: M4.IN2, U5.OUT4

custom parts:
  LuaNode32 / ESP32: New Image for LuaNode32 DOIT ESP32 DEVKIT V1. Base parts from LuaNode32 / ESP32 ESP32 based LuaNode32 by G.Noorlander DOIT Esp32 DevKit v1 (30 pins long, 11 pins width) by Werner Rothschopf (modified by vanepp Dec 2018)
  Texas Instruments DRV8833: The DRV8833 provides a dual bridge motor driver solution for toys, printers, and other mechatronic applications.
  ky-033: KY-033 Line successor module with TCRT5000 and analog output.
  Adafruit TCS34725 RGB Color Sensor: Your electronics can now see in dazzling color with this lovely color light sensor. We found the best color sensor on the market, the TCS34725, which has RGB and Clear light sensing elements. An IR blocking filter, integrated on-chip and localized to the color sensing photodiodes, minimizes the IR spectral component of the incoming light and allows color measurements to be made accurately. The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
